// Logisim project guia0603.circ as structural Verilog: 1 circuit, main circuit main
module main (
  input  X,
  input  Y,
  input  W,
  input  Z,
  input  X_2,
  input  Y_2,
  input  W_2,
  input  Z_2,
  input  X_3,
  input  Y_3,
  input  W_3,
  input  Z_3,
  input  X_4,
  input  Y_4,
  input  W_4,
  input  Z_4,
  input  X_5,
  input  Y_5,
  input  W_5,
  input  Z_5,
  output out_21,
  output out_22,
  output out_23,
  output out_24,
  output out_25
);

  wire and_1_out, and_2_out, and_3_out, and_4_out, and_5_out, and_6_out, and_7_out, and_8_out, and_9_out,
       and_10_out, and_11_out, and_12_out, and_13_out, and_14_out, and_15_out, and_16_out, and_17_out,
       and_18_out, and_19_out, and_20_out, and_21_out, not_1_out, not_2_out, not_3_out, not_4_out, not_5_out,
       not_6_out, not_7_out, not_8_out, not_9_out, not_10_out, not_11_out, not_12_out, not_13_out,
       not_14_out, not_15_out, not_16_out, not_17_out, not_18_out, not_19_out, not_20_out, not_21_out,
       not_22_out, not_23_out, not_24_out, not_25_out, not_26_out, not_27_out, not_28_out, not_29_out,
       not_30_out, not_31_out, not_32_out, not_33_out, not_34_out, not_35_out;

  not not_1 (not_1_out, X_2);
  not not_2 (not_2_out, W_2);
  not not_3 (not_3_out, W_2);
  not not_4 (not_4_out, Y_2);
  not not_5 (not_5_out, Z_2);
  not not_6 (not_6_out, X_2);
  not not_7 (not_7_out, Y_2);
  not not_8 (not_8_out, Z_2);
  not not_9 (not_9_out, X_3);
  not not_10 (not_10_out, W_3);
  not not_11 (not_11_out, Y_3);
  not not_12 (not_12_out, W_3);
  not not_13 (not_13_out, Y_3);
  not not_14 (not_14_out, X_3);
  not not_15 (not_15_out, X_5);
  not not_16 (not_16_out, Y_5);
  not not_17 (not_17_out, W_5);
  not not_18 (not_18_out, Y_5);
  not not_19 (not_19_out, X_5);
  not not_20 (not_20_out, Z_5);
  and and_1 (and_1_out, not_1_out, not_2_out, Z_2);
  and and_2 (and_2_out, Y_2, not_3_out, Z_2);
  and and_3 (and_3_out, X_2, not_4_out, not_5_out);
  and and_4 (and_4_out, not_6_out, not_7_out, W_2, not_8_out);
  and and_5 (and_5_out, not_9_out, not_10_out, not_11_out);
  and and_6 (and_6_out, Y_3, not_12_out, Z_3);
  and and_7 (and_7_out, not_13_out, W_3, Z_3);
  and and_8 (and_8_out, not_14_out, W_3, Z_3);
  and and_9 (and_9_out, not_15_out, not_16_out, not_17_out);
  and and_10 (and_10_out, Y_5, W_5, Z_5);
  and and_11 (and_11_out, X_5, not_18_out, Z_5);
  and and_12 (and_12_out, not_19_out, W_5, not_20_out);
  or or_1 (out_21, and_1_out, and_2_out, and_3_out, and_4_out);
  or or_2 (out_23, and_5_out, and_6_out, and_7_out, and_8_out);
  or or_3 (out_25, and_9_out, and_10_out, and_11_out, and_12_out);
  not not_21 (not_21_out, X);
  not not_22 (not_22_out, W);
  not not_23 (not_23_out, X);
  not not_24 (not_24_out, W);
  not not_25 (not_25_out, X);
  not not_26 (not_26_out, Y);
  not not_27 (not_27_out, Z);
  not not_28 (not_28_out, Z);
  not not_29 (not_29_out, Y_4);
  not not_30 (not_30_out, W_4);
  not not_31 (not_31_out, Z_4);
  not not_32 (not_32_out, X_4);
  not not_33 (not_33_out, W_4);
  not not_34 (not_34_out, Y_4);
  not not_35 (not_35_out, X_4);
  and and_13 (and_13_out, not_21_out, Y, not_22_out);
  and and_14 (and_14_out, not_23_out, Y, Z);
  and and_15 (and_15_out, X, not_24_out, Z);
  and and_16 (and_16_out, not_25_out, not_26_out, W, not_27_out);
  and and_17 (and_17_out, X, Y, W, not_28_out);
  and and_18 (and_18_out, X_4, not_29_out, not_30_out);
  and and_19 (and_19_out, X_4, Y_4, not_31_out);
  and and_20 (and_20_out, not_32_out, not_33_out, not_34_out);
  and and_21 (and_21_out, not_35_out, W_4, Z_4);
  or or_4 (out_22, and_13_out, and_14_out, and_15_out, and_16_out, and_17_out);
  or or_5 (out_24, and_18_out, and_19_out, and_20_out, and_21_out);

  // Notes on the sheet:
  //   a) SoP = m(1,2,5,8,10,13)
  //   b) SoP = m(0,1,3,5,7,11,13)
  //   c) SoP = m(0,1,2,6,7,9,11,15)
  //   d) SoP = m(2,4,5,7,9,13,14)
  //   e) SoP = m(0,1,3,7,8,9,12,14)
endmodule
