// Logisim project guia0604.circ as structural Verilog: 1 circuit, main circuit main
module main (
  input  x,
  input  y,
  input  w,
  input  z,
  input  x_2,
  input  y_2,
  input  w_2,
  input  z_2,
  input  x_3,
  input  y_3,
  input  w_3,
  input  z_3,
  input  x_4,
  input  y_4,
  input  w_4,
  input  z_4,
  input  x_5,
  input  y_5,
  input  w_5,
  input  z_5,
  output out_21,
  output out_22,
  output out_23,
  output out_24,
  output out_25
);

  wire not_1_out, not_2_out, not_3_out, not_4_out, not_5_out, not_6_out, not_7_out, not_8_out, not_9_out,
       not_10_out, not_11_out, not_12_out, not_13_out, not_14_out, not_15_out, not_16_out, not_17_out,
       not_18_out, not_19_out, not_20_out, not_21_out, not_22_out, not_23_out, not_24_out, not_25_out,
       not_26_out, not_27_out, not_28_out, not_29_out, or_1_out, or_2_out, or_3_out, or_4_out, or_5_out,
       or_6_out, or_7_out, or_8_out, or_9_out, or_10_out, or_11_out, or_12_out, or_13_out, or_14_out,
       or_15_out;

  not not_1 (not_1_out, w);
  or or_1 (or_1_out, x, not_1_out, z);
  or or_2 (or_2_out, x, not_2_out, not_3_out);
  not not_2 (not_2_out, y);
  not not_3 (not_3_out, w);
  not not_4 (not_4_out, x);
  not not_5 (not_5_out, y);
  or or_3 (or_3_out, not_4_out, not_5_out, w, not_6_out);
  not not_6 (not_6_out, z);
  not not_7 (not_7_out, x_3);
  or or_4 (or_4_out, not_7_out, y_3, not_8_out);
  not not_8 (not_8_out, z_3);
  not not_9 (not_9_out, y_3);
  not not_10 (not_10_out, w_3);
  or or_5 (or_5_out, not_9_out, not_10_out, not_11_out);
  not not_11 (not_11_out, z_3);
  not not_12 (not_12_out, y_3);
  or or_6 (or_6_out, x_3, not_12_out, w_3, z_3);
  not not_13 (not_13_out, y_5);
  or or_7 (or_7_out, not_13_out, w_5, z_5);
  not not_14 (not_14_out, x_5);
  or or_8 (or_8_out, not_14_out, w_5, z_5);
  not not_15 (not_15_out, x_5);
  not not_16 (not_16_out, y_5);
  or or_9 (or_9_out, not_15_out, not_16_out, not_17_out);
  not not_17 (not_17_out, z_5);
  and and_1 (out_23, or_4_out, or_5_out, or_6_out);
  and and_2 (out_25, or_7_out, or_8_out, or_9_out);
  and and_3 (out_21, or_1_out, or_2_out, or_3_out);
  not not_18 (not_18_out, y_2);
  not not_19 (not_19_out, w_2);
  not not_20 (not_20_out, x_2);
  not not_21 (not_21_out, y_2);
  not not_22 (not_22_out, z_2);
  not not_23 (not_23_out, z_2);
  not not_24 (not_24_out, y_4);
  not not_25 (not_25_out, w_4);
  not not_26 (not_26_out, y_4);
  not not_27 (not_27_out, z_4);
  not not_28 (not_28_out, w_4);
  not not_29 (not_29_out, z_4);
  or or_10 (or_10_out, not_18_out, not_19_out, z_2);
  or or_11 (or_11_out, not_20_out, not_21_out, not_22_out);
  or or_12 (or_12_out, x_2, w_2, not_23_out);
  or or_13 (or_13_out, not_24_out, not_25_out, z_4);
  or or_14 (or_14_out, x_4, not_26_out, not_27_out);
  or or_15 (or_15_out, y_4, not_28_out, not_29_out);
  and and_4 (out_22, or_10_out, or_11_out, or_12_out);
  and and_5 (out_24, or_13_out, or_14_out, or_15_out);

  // Notes on the sheet:
  //   a) PoS = m(2,6,7,13)
  //   b) PoS = m(4,7,9,11,15)
  //   c) PoS = m(4,8,12,13,15)
  //   d) PoS = m(1,5,6,13,14,15)
  //   e) PoS = m(3,5,6,7,11,14)
endmodule
