// Logisim project Guia0801_v1.circ as structural Verilog: 1 circuit, main circuit main
module main (
  input  a5,
  input  a4,
  input  a3,
  input  a2,
  input  a1,
  input  a0,
  input  b5,
  input  b4,
  input  b3,
  input  b2,
  input  b1,
  input  b0,
  input  carry_0,
  output s6,
  output s5,
  output s4,
  output s3,
  output s2,
  output s1,
  output s0,
  output carry_6,
  output carry_5,
  output carry_4,
  output carry_3,
  output carry_2,
  output carry_1
);

  wire and_1_out, and_2_out, and_3_out, and_4_out, and_5_out, and_6_out, and_7_out, and_8_out, and_9_out,
       and_10_out, and_11_out, and_12_out, xor_1_out, xor_2_out, xor_3_out, xor_4_out, xor_5_out, xor_6_out;

  xor xor_1 (xor_1_out, a5, b5);
  xor xor_2 (xor_2_out, a4, b4);
  xor xor_3 (xor_3_out, a3, b3);
  xor xor_4 (xor_4_out, a2, b2);
  xor xor_5 (xor_5_out, a1, b1);
  xor xor_6 (xor_6_out, a0, b0);
  and and_1 (and_1_out, a0, b0);
  xor xor_7 (s5, carry_5, xor_1_out);
  and and_2 (and_2_out, a5, b5);
  xor xor_8 (s4, carry_4, xor_2_out);
  and and_3 (and_3_out, a4, b4);
  xor xor_9 (s3, carry_3, xor_3_out);
  and and_4 (and_4_out, a3, b3);
  xor xor_10 (s2, carry_2, xor_4_out);
  and and_5 (and_5_out, a2, b2);
  xor xor_11 (s1, carry_1, xor_5_out);
  and and_6 (and_6_out, a1, b1);
  xor xor_12 (s0, carry_0, xor_6_out);
  and and_7 (and_7_out, carry_0, xor_6_out);
  or or_1 (carry_1, and_7_out, and_1_out);
  and and_8 (and_8_out, carry_1, xor_5_out);
  and and_9 (and_9_out, carry_2, xor_4_out);
  or or_2 (carry_2, and_8_out, and_6_out);
  and and_10 (and_10_out, carry_3, xor_3_out);
  or or_3 (carry_3, and_9_out, and_5_out);
  or or_4 (carry_4, and_10_out, and_4_out);
  and and_11 (and_11_out, carry_4, xor_2_out);
  or or_5 (carry_5, and_11_out, and_3_out);
  and and_12 (and_12_out, carry_5, xor_1_out);
  or or_6 (carry_6, and_12_out, and_2_out);

  assign s6 = carry_6;
endmodule
