// Logisim project q01.circ as structural Verilog: 1 circuit, main circuit main
module main (
  input  A,
  input  B,
  input  C,
  input  D,
  output out_5,
  output out_6,
  output out_7,
  output out_8,
  output out_9,
  output out_10
);

  wire and_1_out, and_2_out, and_3_out, and_4_out, and_5_out, and_6_out, and_7_out, and_8_out, and_10_out,
       and_11_out, and_12_out, nand_1_out, nand_2_out, nand_3_out, nor_1_out, nor_2_out, nor_3_out,
       not_1_out, not_2_out, not_3_out, not_4_out, not_5_out, not_6_out, not_7_out, not_8_out, not_9_out,
       not_10_out, not_11_out, not_12_out, not_13_out, not_14_out, not_15_out, not_16_out, not_17_out,
       not_18_out, not_19_out, not_20_out, not_21_out, not_22_out, not_23_out, not_24_out, not_25_out,
       not_26_out, not_27_out, not_28_out, not_29_out, not_30_out, not_31_out, not_32_out, not_33_out,
       not_34_out, not_35_out, not_36_out, not_37_out, not_38_out, not_39_out, not_40_out, not_41_out,
       not_42_out, or_1_out, or_2_out, or_3_out, or_4_out, or_5_out, or_6_out, or_7_out, or_8_out, or_11_out,
       or_12_out, or_13_out;

  not not_1 (not_1_out, A);
  not not_2 (not_2_out, B);
  and and_1 (and_1_out, not_1_out, not_2_out, C, D);
  not not_3 (not_3_out, A);
  not not_4 (not_4_out, B);
  and and_2 (and_2_out, not_3_out, not_4_out, C, not_5_out);
  not not_5 (not_5_out, D);
  not not_6 (not_6_out, A);
  and and_3 (and_3_out, not_6_out, B, not_7_out, not_8_out);
  not not_7 (not_7_out, C);
  not not_8 (not_8_out, D);
  not not_9 (not_9_out, A);
  and and_4 (and_4_out, not_9_out, B, not_10_out, D);
  not not_10 (not_10_out, C);
  and and_5 (and_5_out, A, B, not_11_out, D);
  not not_11 (not_11_out, C);
  and and_6 (and_6_out, A, B, C, D);
  not not_12 (not_12_out, B);
  and and_7 (and_7_out, A, not_12_out, C, D);
  not not_13 (not_13_out, B);
  and and_8 (and_8_out, A, not_13_out, C, not_14_out);
  not not_14 (not_14_out, D);
  or or_1 (or_1_out, A, B, C, D);
  or or_2 (or_2_out, A, B, C, not_15_out);
  not not_15 (not_15_out, D);
  not not_16 (not_16_out, B);
  or or_3 (or_3_out, A, not_16_out, not_17_out, not_18_out);
  not not_17 (not_17_out, C);
  not not_18 (not_18_out, D);
  not not_19 (not_19_out, B);
  or or_4 (or_4_out, A, not_19_out, not_20_out, D);
  not not_20 (not_20_out, C);
  not not_21 (not_21_out, A);
  not not_22 (not_22_out, B);
  or or_5 (or_5_out, not_21_out, not_22_out, C, D);
  not not_23 (not_23_out, A);
  not not_24 (not_24_out, B);
  or or_6 (or_6_out, not_23_out, not_24_out, not_25_out, D);
  not not_25 (not_25_out, C);
  not not_26 (not_26_out, A);
  or or_7 (or_7_out, not_26_out, B, C, D);
  not not_27 (not_27_out, A);
  or or_8 (or_8_out, not_27_out, B, C, not_28_out);
  not not_28 (not_28_out, D);
  or or_9 (out_6, and_1_out, and_2_out, and_3_out, and_4_out, and_5_out, and_6_out, and_7_out, and_8_out);
  and and_9 (out_9, or_1_out, or_2_out, or_3_out, or_4_out, or_5_out, or_6_out, or_7_out, or_8_out);
  not not_29 (not_29_out, A);
  not not_30 (not_30_out, C);
  not not_31 (not_31_out, B);
  not not_32 (not_32_out, B);
  not not_33 (not_33_out, C);
  not not_34 (not_34_out, A);
  not not_35 (not_35_out, B);
  not not_36 (not_36_out, A);
  not not_37 (not_37_out, C);
  not not_38 (not_38_out, B);
  not not_39 (not_39_out, B);
  not not_40 (not_40_out, C);
  not not_41 (not_41_out, A);
  not not_42 (not_42_out, B);
  and and_10 (and_10_out, not_29_out, B, not_30_out);
  or or_10 (out_5, and_10_out, and_11_out, and_12_out);
  and and_11 (and_11_out, A, B, D);
  and and_12 (and_12_out, not_31_out, C);
  or or_11 (or_11_out, B, C);
  and and_13 (out_7, or_11_out, or_12_out, or_13_out);
  or or_12 (or_12_out, A, not_32_out, not_33_out);
  or or_13 (or_13_out, not_34_out, not_35_out, D);
  nand nand_1 (nand_1_out, not_36_out, B, not_37_out);
  nand nand_2 (nand_2_out, A, B, D);
  nand nand_3 (nand_3_out, not_38_out, C);
  nor nor_1 (nor_1_out, B, C);
  nor nor_2 (nor_2_out, A, not_39_out, not_40_out);
  nor nor_3 (nor_3_out, not_41_out, not_42_out, D);
  nand nand_4 (out_8, nand_1_out, nand_2_out, nand_3_out);
  nor nor_4 (out_10, nor_1_out, nor_2_out, nor_3_out);

  // Notes on the sheet:
  //   a.)
  //   b.)
  //   c.)
  //   d.)
  //   e.)
  //   f.)
endmodule
