// Logisim project q03.circ as structural Verilog: 1 circuit, main circuit main
module main (
  input  a,
  input  b,
  input  c,
  input  a_2,
  input  b_2,
  output out_6,
  output out_7
);

  wire multiplexer_1_out, multiplexer_2_out, nand_1_out, nand_2_out, nor_1_out, nor_2_out, not_1_out,
       not_2_out, not_3_out;

  nor nor_1 (nor_1_out, a_2, a_2);
  nand nand_1 (nand_1_out, nor_1_out, b_2);
  nor nor_2 (nor_2_out, a_2, a_2);
  nand nand_2 (nand_2_out, nor_2_out, b_2);
  nand nand_3 (out_6, nand_1_out, nand_2_out);
  Multiplexer #(.enable("false")) multiplexer_1 (.in0(b), .in1(not_1_out), .out(multiplexer_1_out), .sel(c));
  not not_1 (not_1_out, b);
  not not_2 (not_2_out, b);
  Multiplexer #(.enable("false")) multiplexer_2 (.in0(not_2_out), .in1(b), .out(multiplexer_2_out), .sel(not_3_out));
  not not_3 (not_3_out, c);
  Multiplexer #(.enable("false")) multiplexer_3 (
    .in0(multiplexer_1_out), .in1(multiplexer_2_out), .out(out_7), .sel(a));

  // Notes on the sheet:
  //   a.)
  //   b.)
endmodule
