// Logisim project Guia_0505.circ as structural Verilog: 1 circuit, main circuit main
module main (
  input  A,
  input  B,
  output out_3
);

  wire not_a_out, x_out, y_out, z_out;

  nor not_a (not_a_out, A, A);
  nor x (x_out, A, B);
  nor z (z_out, not_a_out, y_out);
  nor y (y_out, x_out, x_out);
  nor nor_1 (out_3, z_out, z_out);

  // Notes on the sheet:
  //   Guia_0505$Luís Augusto Lima de Oliveira$Matricula: 805413
  //   ~(a^b) = a xnor b  apenas utilizando portas nativas nor
  //   SoP = m(0, 1, 2, 3)   Pos()      -      são equivalentes
endmodule
