// Logisim project Guia_0506.circ as structural Verilog: 1 circuit, main circuit main
module main (
  input  A,
  input  B,
  output out_3
);

  wire not_A_out, x_out, y_out;

  nand not_A (not_A_out, A, A);
  nand x (x_out, A, B);
  nand s (out_3, not_A_out, y_out);
  nand y (y_out, x_out, x_out);

  // Notes on the sheet:
  //   SoP = m(0, 1, 2, 3)   Pos()      -      são equivalentes
  //   Guia_0506$Luís Augusto Lima de Oliveira$Matricula: 805413
  //   (a^b) = a nor b  apenas utilizando portas nativas nand
endmodule
