// Logisim project Guia_0507.circ as structural Verilog: 1 circuit, main circuit main
module main (
  input  A,
  input  B,
  output out_3
);

  wire Nor_NotA_b_out, Nor_NotB_a_out, Nor_x_out, Nor_y_out, Not_a_out, Not_b_out;

  nor Not_a (Not_a_out, A, A);
  nor Not_b (Not_b_out, B, B);
  nor Nor_NotA_b (Nor_NotA_b_out, Not_a_out, B);
  nor Nor_NotB_a (Nor_NotB_a_out, A, Not_b_out);
  nor Nor_y (Nor_y_out, B, A);
  nor Nor_x (Nor_x_out, Nor_NotA_b_out, Nor_NotB_a_out);
  nor Nor_xy (out_3, Nor_x_out, Nor_y_out);

  // Notes on the sheet:
  //   SoP = m(1,2)
  //   ~(a^~b) apenas com portas nor
  //   Guia_0507$Luís Augusto Lima de Oliveira$Matricula: 805413
  //   PoS = m(0,3)
endmodule
