// Logisim project Guia0701.circ as structural Verilog: 1 circuit, main circuit main
module main (
  input  x,
  input  y,
  input  e,
  output x_y,
  output n_x_y,
  output out_6
);

  wire and_2_out, and_3_out, and_4_out, nand_2_out, not_1_out;

  not not_1 (not_1_out, e);
  and and_1 (x_y, x, y);
  nand nand_1 (n_x_y, x, y);
  and and_2 (and_2_out, x, y);
  nand nand_2 (nand_2_out, x, y);
  and and_3 (and_3_out, and_2_out, not_1_out);
  and and_4 (and_4_out, nand_2_out, e);
  or or_1 (out_6, and_3_out, and_4_out);

  // Notes on the sheet:
  //   1-Nand$0-And
endmodule
