// Logisim project Guia0703.circ as structural Verilog: 1 circuit, main circuit main
module main (
  input  x,
  input  y,
  input  S,
  input  Sgrupo,
  output out_5
);

  wire and_1_out, and_2_out, and_3_out, and_4_out, and_5_out, and_6_out, and_7_out, nand_1_out, nor_1_out,
       not_1_out, not_2_out, not_3_out, or_1_out, or_2_out, or_3_out;

  or or_1 (or_1_out, x, y);
  not not_1 (not_1_out, S);
  nor nor_1 (nor_1_out, x, y);
  and and_1 (and_1_out, x, y);
  nand nand_1 (nand_1_out, x, y);
  and and_2 (and_2_out, or_1_out, not_1_out);
  and and_3 (and_3_out, S, nor_1_out);
  and and_4 (and_4_out, and_1_out, not_2_out);
  not not_2 (not_2_out, S);
  and and_5 (and_5_out, S, nand_1_out);
  or or_2 (or_2_out, and_2_out, and_3_out);
  not not_3 (not_3_out, Sgrupo);
  or or_3 (or_3_out, and_4_out, and_5_out);
  and and_6 (and_6_out, or_2_out, not_3_out);
  and and_7 (and_7_out, Sgrupo, or_3_out);
  or or_4 (out_5, and_6_out, and_7_out);

  // Notes on the sheet:
  //   x+y
  //   ~(x+y)
  //   x.y
  //   ~(x.y)
  //   1 - Nor$0 - Or
  //   1 - Nand$0 - And
  //   Nand/And
  //   Nor/Or
  //   Previsão:$Se s=0 e Sgrupo=0   SoP(x,y) = m(1,2,3)$Se s=1 e Sgrupo=0   SoP(x,y) = m(0)$Se s=0 e Sgrupo=1   SoP(x,y) = m(3)$Se s=1 e Sgrupo=0   SoP(x,y) = m(0,1,2)
endmodule
