// Logisim project Guia0801_v1.circ as structural Verilog: 1 circuit, main circuit main
module main (
  input  [4:0] a,
  input  [4:0] b,
  input  carry_0,
  output S5,
  output S4,
  output S3,
  output S2,
  output S1,
  output S0,
  output carry_5,
  output carry_4,
  output carry_3,
  output carry_2,
  output carry_1
);

  wire and_1_out, and_2_out, and_3_out, and_4_out, and_5_out, and_6_out, and_7_out, and_8_out, and_9_out,
       and_10_out, xor_2_out, xor_4_out, xor_6_out, xor_8_out, xor_10_out;

  xor xor_1 (S4, carry_4, xor_2_out);
  xor xor_2 (xor_2_out, a[4], b[4]);
  and and_1 (and_1_out, a[4], b[4]);
  xor xor_3 (S3, carry_3, xor_4_out);
  xor xor_4 (xor_4_out, a[3], b[3]);
  and and_2 (and_2_out, a[3], b[3]);
  xor xor_5 (S2, carry_2, xor_6_out);
  xor xor_6 (xor_6_out, a[2], b[2]);
  and and_3 (and_3_out, a[2], b[2]);
  xor xor_7 (S1, carry_1, xor_8_out);
  xor xor_8 (xor_8_out, a[1], b[1]);
  and and_4 (and_4_out, a[1], b[1]);
  xor xor_9 (S0, carry_0, xor_10_out);
  xor xor_10 (xor_10_out, a[0], b[0]);
  and and_5 (and_5_out, a[0], b[0]);
  and and_6 (and_6_out, carry_0, xor_10_out);
  or or_1 (carry_1, and_6_out, and_5_out);
  and and_7 (and_7_out, carry_1, xor_8_out);
  or or_2 (carry_2, and_7_out, and_4_out);
  and and_8 (and_8_out, carry_2, xor_6_out);
  or or_3 (carry_3, and_8_out, and_3_out);
  and and_9 (and_9_out, carry_3, xor_4_out);
  and and_10 (and_10_out, carry_4, xor_2_out);
  or or_4 (carry_4, and_9_out, and_2_out);
  or or_5 (carry_5, and_10_out, and_1_out);

  assign S5 = carry_5;
endmodule
