// Logisim project R_02.circ as structural Verilog: 7 circuits, main circuit R_0204a
module R_0204a (
  input  a,
  input  b,
  input  c,
  output out_4
);

  wire not_1_out, not_2_out;

  not not_1 (not_1_out, a);
  and and_1 (out_4, not_1_out, not_2_out);
  not not_2 (not_2_out, c);
endmodule

module R_0204b (
  input  a,
  input  b,
  input  c,
  output out_4,
  output out_5
);

  wire not_1_out, not_2_out, not_3_out;

  not not_1 (not_1_out, a);
  and Ja (out_4, not_1_out, not_2_out);
  not not_2 (not_2_out, c);
  and Ka (out_5, a, not_3_out);
  not not_3 (not_3_out, c);
endmodule

module R_0204c (
  input  a,
  input  b,
  input  c,
  output out_4
);

  wire and_1_out;

  or or_1 (out_4, a, and_1_out);
  and and_1 (and_1_out, a, a);
endmodule

module R_0204d (
  input  a,
  input  b,
  input  c,
  output out_4,
  output out_5
);

  wire not_1_out, not_2_out, Rb_2_out, Rb_out;

  not not_1 (not_1_out, a);
  not not_2 (not_2_out, c);
  and Sb (out_4, b, c);
  and Rb (Rb_out, not_1_out, b, c);
  and Rb_2 (Rb_2_out, a, b, not_2_out);
  or Rb_3 (out_5, Rb_out, Rb_2_out);
endmodule

module R_0204e (
  input  a,
  input  b,
  input  c,
  output out_4
);

  wire and_1_out, and_2_out, and_3_out, not_1_out, not_2_out;

  and and_1 (and_1_out, a, c);
  and and_2 (and_2_out, a, b, not_1_out);
  not not_1 (not_1_out, c);
  not not_2 (not_2_out, b);
  and and_3 (and_3_out, not_2_out, c);
  or or_1 (out_4, and_1_out, and_2_out, and_3_out);
endmodule

module R_0205a (
  input  a,
  input  b,
  input  c,
  output out_4
);

  wire nand_1_out, nand_2_out, nand_3_out;

  nand nand_1 (nand_1_out, a, a);
  nand nand_2 (nand_2_out, nand_1_out, nand_3_out);
  nand nand_3 (nand_3_out, c, c);
  nand nand_4 (out_4, nand_2_out, nand_2_out);
endmodule

module R_0205b (
  input  a,
  input  b,
  input  c,
  output out_4
);

  wire nor_1_out;

  nor nor_1 (nor_1_out, c, c);
  nor nor_2 (out_4, b, nor_1_out);
endmodule
