// Logisim project q06.circ as structural Verilog: 1 circuit, main circuit main
module main (
  input  in_1,
  input  Load
);

  wire clock_1_out, t_ff_1_q, t_ff_2_q;

  Clock clock_1 (.out(clock_1_out));
  T_Flip_Flop #(.Pre_Clr_Positions("LEGACY"), .NewFFLayout("false")) t_ff_1 (
    .clk(clock_1_out), .T(in_1), .Q(t_ff_1_q), .reset(Load));  // open: Qn, preset
  T_Flip_Flop #(.Pre_Clr_Positions("LEGACY"), .NewFFLayout("false")) t_ff_2 (
    .clk(clock_1_out), .T(t_ff_1_q), .Q(t_ff_2_q), .preset(Load));  // open: Qn, reset
  T_Flip_Flop #(.Pre_Clr_Positions("LEGACY"), .NewFFLayout("false")) t_ff_3 (
    .clk(clock_1_out), .T(t_ff_2_q), .preset(Load));  // open: Q, Qn, reset
endmodule
