// Logisim project ULA.circ as structural Verilog: 6 circuits, main circuit ULA_4bits
module ULA_1bits (
  input  Binvert,
  input  CarryIn,
  input  o1,
  input  o0,
  input  A,
  input  B,
  output result,
  output CarryOut
);

  wire and_1_out, mux_binvert_1_out_4, not_1_out, not_2_out, or_1_out, soma_completa_1_s0;

  Mux_Binvert mux_binvert_1 (.x0(B), .x1(not_1_out), .o(Binvert), .out_4(mux_binvert_1_out_4));
  not not_1 (not_1_out, B);
  and and_1 (and_1_out, A, mux_binvert_1_out_4);
  or or_1 (or_1_out, A, mux_binvert_1_out_4);
  not not_2 (not_2_out, A);
  Soma_Completa soma_completa_1 (
    .x(A), .y(mux_binvert_1_out_4), .carry_in(CarryIn), .s0(soma_completa_1_s0), .carry_out(CarryOut));
  Mux mux_1 (.x0(and_1_out), .x1(or_1_out), .x2(not_2_out), .x3(soma_completa_1_s0), .o1(o1), .o0(o0), .out_7(result));
endmodule

module Meia_soma (
  input  x0,
  input  y0,
  output s0,
  output carry_out
);

  xor xor_1 (s0, y0, x0);
  and and_1 (carry_out, y0, x0);
endmodule

module Soma_Completa (
  input  x,
  input  y,
  input  carry_in,
  output s0,
  output carry_out
);

  wire meia_soma_1_p1, meia_soma_1_p4, meia_soma_2_p4;

  // SOMADOR_Meia_soma meia_soma_1: pin names not known; wires that end beside it: meia_soma_1_p1, carry_in, s0, meia_soma_1_p4
  // SOMADOR_Meia_soma meia_soma_2: pin names not known; wires that end beside it: x, y, meia_soma_1_p1, meia_soma_2_p4
  or or_1 (carry_out, meia_soma_1_p4, meia_soma_2_p4);
endmodule

module Mux (
  input  o1,
  input  o0,
  input  x0,
  input  x1,
  input  x2,
  input  x3,
  output out_7
);

  wire and_1_out, and_2_out, and_3_out, and_4_out, not_1_out, not_2_out, not_3_out, not_4_out;

  not not_1 (not_1_out, o1);
  not not_2 (not_2_out, o0);
  not not_3 (not_3_out, o1);
  not not_4 (not_4_out, o0);
  and and_1 (and_1_out, x0, not_1_out, not_2_out);
  and and_2 (and_2_out, x1, not_3_out, o0);
  or or_1 (out_7, and_1_out, and_2_out, and_3_out, and_4_out);
  and and_3 (and_3_out, x2, o1, not_4_out);
  and and_4 (and_4_out, x3, o1, o0);
endmodule

module Mux_Binvert (
  input  o,
  input  x0,
  input  x1,
  output out_4
);

  wire and_1_out, and_2_out, not_1_out;

  not not_1 (not_1_out, o);
  and and_1 (and_1_out, x0, not_1_out);
  or or_1 (out_4, and_1_out, and_2_out);
  and and_2 (and_2_out, x1, o);
endmodule

module ULA_4bits (
  input  o1,
  input  o0,
  input  B3,
  input  B2,
  input  B1,
  input  B0,
  input  A3,
  input  A2,
  input  A1,
  input  A0,
  input  Binvert,
  output S0,
  output S1,
  output S2,
  output S3,
  output Cout
);

  wire ula_1bits_1_carryout, ula_1bits_2_carryout, ula_1bits_3_carryout;

  ULA_1bits ula_1bits_1 (
    .A(A0), .B(B0), .Binvert(Binvert), .CarryIn(Binvert), .o1(o1), .o0(o0), .CarryOut(ula_1bits_1_carryout),
    .result(S0));
  ULA_1bits ula_1bits_2 (
    .A(A1), .B(B1), .Binvert(Binvert), .CarryIn(ula_1bits_1_carryout), .o1(o1), .o0(o0),
    .CarryOut(ula_1bits_2_carryout), .result(S1));
  ULA_1bits ula_1bits_3 (
    .A(A2), .B(B2), .Binvert(Binvert), .CarryIn(ula_1bits_2_carryout), .o1(o1), .o0(o0),
    .CarryOut(ula_1bits_3_carryout), .result(S2));
  ULA_1bits ula_1bits_4 (
    .A(A3), .B(B3), .Binvert(Binvert), .CarryIn(ula_1bits_3_carryout), .o1(o1), .o0(o0), .CarryOut(Cout),
    .result(S3));
endmodule
