// Logisim project Guia_0501.circ as structural Verilog: 1 circuit, main circuit main
module main (
  input  A,
  input  B,
  output out_3
);

  nor nor_1 (out_3, A, B);

  // Notes on the sheet:
  //   SoP = m ( 0 )
  //   Guia_0501$Luís Augusto Lima de Oliveira$Matricula: 805413
  //   (~a & ~b) utilizando apenas portas nor
  //   (~a & ~b) = ~(a | b)
  //   PoS = m( 1, 2, 3 )
endmodule
