// Logisim project Guia_0502.circ as structural Verilog: 1 circuit, main circuit main
module main (
  input  A,
  input  B,
  output out_3
);

  wire nand_1_out;

  nand nand_1 (nand_1_out, A, A);
  nand nand_2 (out_3, nand_1_out, B);

  // Notes on the sheet:
  //   SoP = m ( 0, 2, 3 )
  //   Guia_0502$Luís Augusto Lima de Oliveira$Matricula: 805413
  //   (a | ~b) apenas com portas nand
  //   (a | ~b) equivale à ~(~a & b)
  //   PoS = m ( 1 )
endmodule
