// Logisim project Guia_0503.circ as structural Verilog: 1 circuit, main circuit main
module main (
  input  A,
  input  B,
  output out_3
);

  wire nor_1_out, nor_2_out, nor_3_out;

  nor nor_1 (nor_1_out, A, A);
  nor nor_2 (nor_2_out, B, B);
  nor nor_3 (nor_3_out, nor_1_out, nor_2_out);
  nor nor_4 (out_3, nor_3_out, nor_3_out);

  // Notes on the sheet:
  //   SoP = m( 0, 1, 2 )
  //   Guia_0503$Luís Augusto Lima de Oliveira$Matricula: 805413
  //   (~a | ~b) apenas com portas nor
  //   PoS = m( 3 )
endmodule
