// Logisim project Guia_0508.circ as structural Verilog: 1 circuit, main circuit main
module main (
  input  A,
  input  B,
  output out_3
);

  wire nand_1_out;

  nand nand_1 (nand_1_out, B, B);
  nand nand_2 (out_3, A, nand_1_out);

  // Notes on the sheet:
  //   SoP = m(0, 1, 3) 
  //   Guia_0508$Luís Augusto Lima de Oliveira$Matricula: 805413
  //   ~(a & ~b) apenas com portas nand
  //   PoS = m(2)
endmodule
