// Logisim project guia0602.circ as structural Verilog: 1 circuit, main circuit main
module main (
  input  x,
  input  y,
  input  z,
  input  x_2,
  input  y_2,
  input  z_2,
  input  x_3,
  input  y_3,
  input  z_3,
  input  x_4,
  input  y_4,
  input  z_4,
  input  x_5,
  input  y_5,
  input  z_5,
  output out_16,
  output out_17,
  output out_18,
  output out_19,
  output out_20
);

  wire not_1_out, not_2_out, not_3_out, not_4_out, not_5_out, not_6_out, not_7_out, not_8_out, not_9_out,
       not_10_out, not_11_out, not_12_out, not_13_out, not_14_out, not_15_out, not_16_out, or_1_out,
       or_2_out, or_3_out, or_4_out, or_5_out, or_6_out, or_7_out, or_8_out, or_9_out, or_10_out, or_11_out;

  not not_1 (not_1_out, x);
  or or_1 (or_1_out, not_1_out, not_2_out);
  not not_2 (not_2_out, z);
  not not_3 (not_3_out, x);
  or or_2 (or_2_out, not_3_out, y);
  not not_4 (not_4_out, y_4);
  or or_3 (or_3_out, not_4_out, z_4);
  not not_5 (not_5_out, x_4);
  or or_4 (or_4_out, not_5_out, y_4, not_6_out);
  not not_6 (not_6_out, z_4);
  or or_5 (or_5_out, x_5, not_7_out);
  not not_7 (not_7_out, y_5);
  not not_8 (not_8_out, x_5);
  or or_6 (or_6_out, not_8_out, not_9_out);
  not not_9 (not_9_out, z_5);
  and and_1 (out_16, or_1_out, or_2_out);
  and and_2 (out_19, or_3_out, or_4_out);
  and and_3 (out_20, or_5_out, or_6_out);
  not not_10 (not_10_out, y_2);
  not not_11 (not_11_out, x_2);
  not not_12 (not_12_out, z_2);
  not not_13 (not_13_out, y_3);
  not not_14 (not_14_out, x_3);
  not not_15 (not_15_out, x_3);
  not not_16 (not_16_out, y_3);
  or or_7 (or_7_out, x_2, not_10_out);
  and and_4 (out_17, or_7_out, or_8_out);
  or or_8 (or_8_out, not_11_out, not_12_out);
  or or_9 (or_9_out, not_13_out, z_3);
  or or_10 (or_10_out, not_14_out, z_3);
  and and_5 (out_18, or_9_out, or_10_out, or_11_out);
  or or_11 (or_11_out, not_15_out, not_16_out);

  // Notes on the sheet:
  //   a.) PoS = M(4,5,7)
  //   b.) PoS = M(2,5,6)
  //   c.) PoS = M(2,5,6)
  //   d.) PoS = M(2, 3, 5,7)
  //   e.) PoS = M(2,4,6,7)
endmodule
