// Logisim project guia0606.circ as structural Verilog: 1 circuit, main circuit main
module main (
  input  x,
  input  y,
  input  w,
  input  z,
  input  x_2,
  input  y_2,
  input  w_2,
  input  z_2,
  output out_9,
  output out_10
);

  wire and_1_out, and_2_out, and_4_out, nand_1_out, not_1_out, not_2_out, not_3_out, not_4_out, not_5_out,
       not_6_out, not_7_out, or_1_out, or_2_out;

  not not_1 (not_1_out, y);
  or or_1 (or_1_out, not_1_out, w, not_2_out);
  not not_2 (not_2_out, x);
  and and_1 (and_1_out, y, not_3_out, x);
  not not_3 (not_3_out, w);
  and and_2 (and_2_out, z, w, y);
  not not_4 (not_4_out, x);
  and and_3 (out_10, x_2, nand_1_out);
  nand nand_1 (nand_1_out, x_2, y_2, w_2, z_2);
  not not_5 (not_5_out, or_1_out);
  and and_4 (and_4_out, not_5_out, not_6_out);
  not not_6 (not_6_out, and_1_out);
  not not_7 (not_7_out, or_2_out);
  or or_2 (or_2_out, and_2_out, not_4_out);
  or or_3 (out_9, and_4_out, not_7_out);

  // Notes on the sheet:
  //   PoS = M(0,1,2,3,4,5,6,7,15)
  //   = x.(x'+y'+z'+w')
  //   = x.~(x.y.z.w)
endmodule
