// Logisim project Guia0702.circ as structural Verilog: 1 circuit, main circuit main
module main (
  input  x,
  input  y,
  input  e,
  output out_4
);

  wire and_1_out, and_2_out, nor_1_out, not_1_out, or_1_out;

  or or_1 (or_1_out, x, y);
  not not_1 (not_1_out, e);
  nor nor_1 (nor_1_out, x, y);
  and and_1 (and_1_out, or_1_out, not_1_out);
  and and_2 (and_2_out, e, nor_1_out);
  or or_2 (out_4, and_1_out, and_2_out);

  // Notes on the sheet:
  //   x+y
  //   ~(x+y)
  //   1 - Nor$0 - Or
endmodule
