// Logisim project Guia0704.circ as structural Verilog: 1 circuit, main circuit main
module main (
  input  x,
  input  y,
  input  s_1,
  input  s_0,
  output out_5
);

  wire and_1_out, and_2_out, and_3_out, and_4_out, nor_1_out, not_1_out, not_2_out, or_1_out, xnor_1_out,
       xor_1_out;

  xor xor_1 (xor_1_out, x, y);
  xnor xnor_1 (xnor_1_out, x, y);
  or or_1 (or_1_out, x, y);
  nor nor_1 (nor_1_out, x, y);
  not not_1 (not_1_out, s_1);
  and and_1 (and_1_out, xor_1_out, not_1_out, not_2_out);
  and and_2 (and_2_out, xnor_1_out, not_1_out, s_0);
  and and_3 (and_3_out, or_1_out, s_1, not_2_out);
  and and_4 (and_4_out, nor_1_out, s_1, s_0);
  not not_2 (not_2_out, s_0);
  or or_2 (out_5, and_1_out, and_2_out, and_3_out, and_4_out);

  // Notes on the sheet:
  //   Previsão:$Se s=00    SoP(x,y) = m(1,2)$Se s=01    SoP(x,y) = m(0,3)$Se s=10    SoP(x,y) = m(1,2,3)$Se s=11    SoP(x,y) = m(0)
endmodule
