// Logisim project Guia0705.circ as structural Verilog: 1 circuit, main circuit main
module main (
  input  x,
  input  y,
  input  s_2,
  input  s_1,
  input  s_0,
  output out_6
);

  wire and_1_out, and_2_out, and_3_out, and_4_out, and_5_out, and_6_out, and_7_out, and_8_out, and_9_out,
       nand_1_out, nor_1_out, not_1_out, not_2_out, not_3_out, not_4_out, not_5_out, or_1_out, xnor_1_out,
       xor_1_out;

  not not_1 (not_1_out, x);
  not not_2 (not_2_out, y);
  and and_1 (and_1_out, x, y);
  nand nand_1 (nand_1_out, x, y);
  xor xor_1 (xor_1_out, x, y);
  xnor xnor_1 (xnor_1_out, x, y);
  or or_1 (or_1_out, x, y);
  nor nor_1 (nor_1_out, x, y);
  not not_3 (not_3_out, s_2);
  not not_4 (not_4_out, s_0);
  not not_5 (not_5_out, s_1);
  and and_2 (and_2_out, not_1_out, not_3_out, not_5_out, not_4_out);
  and and_3 (and_3_out, not_2_out, not_3_out, not_5_out, s_0);
  and and_4 (and_4_out, and_1_out, not_3_out, s_1, not_4_out);
  and and_5 (and_5_out, nand_1_out, not_3_out, s_1, s_0);
  and and_6 (and_6_out, xor_1_out, s_2, not_5_out, not_4_out);
  and and_7 (and_7_out, xnor_1_out, s_2, not_5_out, s_0);
  and and_8 (and_8_out, or_1_out, s_2, s_1, not_4_out);
  and and_9 (and_9_out, nor_1_out, s_2, s_1, s_0);
  or or_2 (out_6, and_2_out, and_3_out, and_4_out, and_5_out, and_6_out, and_7_out, and_8_out, and_9_out);

  // Notes on the sheet:
  //   5.) Mux 7x1
  //   Previsão:$Se s=000    SoP(x,y) = m(0,1)$Se s=001    SoP(x,y) = m(0,2)$Se s=010    SoP(x,y) = m(3)$Se s=011    SoP(x,y) = m(0,1,2)$Se s=100    SoP(x,y) = m(1,2)$Se s=101    SoP(x,y) = m(0,3)$Se s=111    SoP(x,y) = m(0)
endmodule
