// Logisim project Guia0804.circ as structural Verilog: 1 circuit, main circuit main
module main (
  input  [4:0] a,
  input  [4:0] b,
  output S4,
  output S3,
  output S2,
  output S1,
  output S0
);

  xor xor_1 (S0, a[0], b[0]);
  xor xor_2 (S1, a[1], b[1]);
  xor xor_3 (S2, a[2], b[2]);
  xor xor_4 (S3, a[3], b[3]);
  xor xor_5 (S4, a[4], b[4]);
endmodule
