// Logisim project q04_a.circ as structural Verilog: 1 circuit, main circuit main
module main (
  input  a,
  input  b,
  input  c,
  output out_4
);

  wire not_1_out, not_2_out;

  not not_1 (not_1_out, a);
  and and_1 (out_4, not_1_out, not_2_out);
  not not_2 (not_2_out, c);
endmodule
