// Logisim project q04_b.circ as structural Verilog: 1 circuit, main circuit main
module main (
  input  a,
  input  b,
  input  c,
  output Ja,
  output ka
);

  wire not_1_out, not_2_out, not_3_out;

  not not_1 (not_1_out, a);
  and and_1 (Ja, not_1_out, not_2_out);
  not not_2 (not_2_out, c);
  and and_2 (ka, a, not_3_out);
  not not_3 (not_3_out, c);
endmodule
