// Logisim project q04_c.circ as structural Verilog: 1 circuit, main circuit main
module main (
  input  a,
  input  b,
  input  c,
  output out_4
);

  wire and_1_out;

  or or_1 (out_4, a, and_1_out);
  and and_1 (and_1_out, a, a);
endmodule
