// Logisim project q04_d.circ as structural Verilog: 1 circuit, main circuit main
module main (
  input  a,
  input  b,
  input  c,
  output out_4,
  output out_5
);

  wire not_1_out, not_2_out, Rb_2_out, Rb_out;

  not not_1 (not_1_out, a);
  not not_2 (not_2_out, c);
  and Sb (out_4, b, c);
  and Rb (Rb_out, not_1_out, b, c);
  and Rb_2 (Rb_2_out, a, b, not_2_out);
  or Rb_3 (out_5, Rb_out, Rb_2_out);
endmodule
