// Logisim project q05_b.circ as structural Verilog: 1 circuit, main circuit main
module main (
  input  a,
  input  b,
  input  c,
  output out_4
);

  wire nor_1_out;

  nor nor_1 (nor_1_out, c, c);
  nor nor_2 (out_4, b, nor_1_out);
endmodule
